# Fritzing sketch irdebug (saved by Fritzing 0.8.7b)
breadboards: 1

parts:
  Arduino = Arduino Uno (Rev3)
  R1 = Resistor [tolerance=±5% resistance=220 package=THT]
  LED = smd LED [color="Red (633nm)" package="0603 [SMD]"]
  IR_LED = LTE-302 [package=lte-302]
  R2 = Resistor [tolerance=±5% resistance=220 package=THT]
  IR1 = TSOP312.., 314.. [package=THT]

nets:
  N1: Arduino.D2, R1.Pin_0, IR1.Data
  N2: Arduino.D3_PWM, IR_LED.A
  N3: Arduino.5V, LED.anode, IR1.Vs
  GND: Arduino.GND, R2.Pin_0, IR1.GND
  N4: R1.Pin_1, LED.cathode
  N5: IR_LED.C, R2.Pin_1
